# Fritzing sketch schaltung (saved by Fritzing 0.9.3b)

parts:
  Raspberry_Pi_1 = Raspberry Pi 3 [part_number=RPI-3-V1.2]
  S10 = Pushbutton [package="[THT]"]
  S11 = Pushbutton [package="[THT]"]
  S12 = Pushbutton [package="[THT]"]
  S13 = Pushbutton [package="[THT]"]
  S14 = Pushbutton [package="[THT]"]
  S15 = Pushbutton [package="[THT]"]
  S16 = Pushbutton [package="[THT]"]
  S17 = Pushbutton [package="[THT]"]
  S18 = Pushbutton [package="[THT]"]

nets:
  3V3: Raspberry_Pi_1.3v3, Raspberry_Pi_1.3V3, S10.Pin_4, S11.Pin_3, S11.Pin_4, S12.Pin_3, S12.Pin_4, S13.Pin_3, S13.Pin_4, S14.Pin_4, S15.Pin_3, S15.Pin_4, S16.Pin_3, S16.Pin_4, S17.Pin_3, S17.Pin_4, S18.Pin_3
  N1: Raspberry_Pi_1.GPIO17, S14.Pin_2
  N2: Raspberry_Pi_1.GPIO27, S13.Pin_2
  N3: Raspberry_Pi_1.GPIO22, S15.Pin_2
  N4: Raspberry_Pi_1.GPIO13, S18.Pin_2
  N5: Raspberry_Pi_1.GPIO19, S16.Pin_2
  N6: Raspberry_Pi_1.GPIO26, S17.Pin_2
  N7: Raspberry_Pi_1.GPIO21, S10.Pin_2
  N8: Raspberry_Pi_1.GPIO20, S12.Pin_2
  N9: Raspberry_Pi_1.GPIO16, S11.Pin_2

notes:
  Buzzer1
  Buzzer2
  Buzzer3
